# Fritzing sketch catamarano (saved by Fritzing 0.8.3b)
breadboards: 1

parts:
  Componente1 = Arduino Uno (Rev3)
  J1 = Basic Servo
  Q1 = Basic FET N-Channel [package="TO220 [THT]"]
  M1 = DC Motor
  D1 = Diode [package=diode-1n4001]

nets:
  5V: Componente1.5V, J1.vcc, Q1.source
  GND: Componente1.GND, J1.gnd
  N1: Componente1.D8, J1.pulse
  N2: Componente1.D5_PWM, Q1.gate, M1.pin_2
  N3: Componente1.VIN, M1.pin_1
  N4: Q1.drain, D1.A
